# Fritzing sketch oegg (saved by Fritzing 0.9.3b)
breadboards: 1

parts:
  元件1 = OLED Monochrome 128x64 0.96 inch [part_number=326]
  元件2 = Arduino Uno (Rev3)
  D1 = LED_BARGRAPH_10 [package=led_bargaph_10]
  R1 = Resistor [tolerance=±5% resistance=220 package=THT]
  R2 = Resistor [tolerance=±5% resistance=220 package=THT]
  R3 = Resistor [tolerance=±5% resistance=220 package=THT]
  R4 = Resistor [tolerance=±5% resistance=220 package=THT]
  R5 = Resistor [tolerance=±5% resistance=220 package=THT]
  R6 = Resistor [tolerance=±5% resistance=220 package=THT]
  R7 = Resistor [tolerance=±5% resistance=220 package=THT]
  R8 = Resistor [tolerance=±5% resistance=220 package=THT]
  J1 = Basic Force Sensing Resistor (FSR) [package=THT]
  R9 = Resistor [tolerance=±5% resistance=220 package=THT]

nets:
  N1: 元件1.MOSI_SDA, 元件2.D12/MISO
  N2: 元件1.SCLK_SCK, 元件2.D11_PWM/MOSI
  N3: 元件1.DC_SA0, 元件2.D9_PWM
  N4: 元件1.RESET, 元件2.D10_PWM/SS
  N5: 元件1.CS, 元件2.D8
  VIN: 元件1.VIN, 元件2.5V, J1.pin_0
  GND: 元件1.GND, 元件2.GND, R1.Pin_1, R2.Pin_1, R3.Pin_1, R4.Pin_1, R5.Pin_1, R6.Pin_1, R7.Pin_1, R8.Pin_1, R9.Pin_1
  N6: 元件2.A0, J1.pin_1, R9.Pin_0
  N7: 元件2.D13/SCK, D1.B_A
  N8: 元件2.D1/TX, D1.I_A
  N9: 元件2.D2, D1.H_A
  N10: 元件2.D3_PWM, D1.G_A
  N11: 元件2.D4, D1.F_A
  N12: 元件2.D5_PWM, D1.E_A
  N13: 元件2.D6_PWM, D1.D_A
  N14: 元件2.D7, D1.C_A
  N15: D1.I_C, R1.Pin_0
  N16: D1.H_C, R2.Pin_0
  N17: D1.G_C, R8.Pin_0
  N18: D1.F_C, R3.Pin_0
  N19: D1.E_C, R5.Pin_0
  N20: D1.D_C, R7.Pin_0
  N21: D1.C_C, R6.Pin_0
  N22: D1.B_C, R4.Pin_0

custom parts:
  OLED Monochrome 128x64 0.96 inch: These displays are small, only about 1" diameter, but very readable due to the high contrast of an OLED display. This display is made of 128x64 individual white OLED pixels, each one is turned on or off by the controller chip. Because the display makes its own light, no backlight is required. This reduces the power required to run the OLED and is why the display has such high contrast; we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
